// Digital circuit ALU.dig as structural Verilog
module ALU (
  input  [23:0] A,
  input  [23:0] B,
  input  [23:0] Data,
  input  Enable,
  input  [3:0] Instruction,
  input  CarryIn,
  output [23:0] REGA,
  output [23:0] REGB,
  output Carry
);

  wire add_1_c_o, Carry_t, not_1_out, sub_1_c_o;
  wire [23:0] add_1_s, B_t, div_1_q, div_1_r, multiplexer_4_out, REGA_t, REGB_t, sub_1_s;
  wire [47:0] mul_1_mul;

  Multiplexer #(.Bits(24)) multiplexer_1 (.sel(Enable), .in_0(A), .in_1(REGA_t), .out(REGA));
  Multiplexer #(.Bits(24)) multiplexer_2 (.sel(Enable), .in_0(B), .in_1(REGB_t), .out(REGB));
  Multiplexer multiplexer_3 (.sel(Enable), .in_0(CarryIn), .in_1(Carry_t), .out(Carry));
  Add #(.Bits(24)) add_1 (.a(A), .b(B_t), .c_i(CarryIn), .s(add_1_s), .c_o(add_1_c_o));
  Sub #(.Bits(24)) sub_1 (.a(A), .b(B_t), .c_i(CarryIn), .s(sub_1_s), .c_o(sub_1_c_o));
  Mul #(.Bits(24)) mul_1 (.a(A), .b(B_t), .mul(mul_1_mul));
  Div #(.Bits(24)) div_1 (.a(A), .b(B_t), .q(div_1_q), .r(div_1_r));
  Multiplexer #(.Bits(24)) multiplexer_4 (.sel(not_1_out), .in_0(mul_1_mul[47:24]), .in_1(B), .out(multiplexer_4_out));
  not not_1 (not_1_out, Instruction[0]);
  Multiplexer #(.Selector_Bits(3), .Bits(24)) multiplexer_5 (
    .sel(Instruction[3:1]), .in_0(mul_1_mul[23:0]), .in_1(add_1_s), .in_2(sub_1_s), .in_3(mul_1_mul[23:0]),
    .in_4(div_1_q), .in_5(div_1_r), .in_6(div_1_q), .in_7(mul_1_mul[23:0]), .out(REGA_t));
  Multiplexer #(.Selector_Bits(3), .Bits(24)) multiplexer_6 (
    .sel(Instruction[3:1]), .in_0(multiplexer_4_out), .in_1(B), .in_2(B), .in_3(B), .in_4(B), .in_5(B),
    .in_6(div_1_r), .in_7(mul_1_mul[47:24]), .out(REGB_t));
  Multiplexer #(.Bits(24)) multiplexer_7 (.sel(Instruction[0]), .in_0(B), .in_1(Data), .out(B_t));
  Multiplexer #(.Selector_Bits(3)) multiplexer_8 (
    .sel(Instruction[3:1]), .in_0(CarryIn), .in_1(add_1_c_o), .in_2(sub_1_c_o), .in_3(CarryIn),
    .in_4(CarryIn), .in_5(CarryIn), .in_6(CarryIn), .in_7(CarryIn), .out(Carry_t));

  // Other names for the same wires on the sheet: AFlag = Instruction[0]; Operation[2:0] = Instruction[3:1];
  //   TrueB[23:0] = B
endmodule
