// Digital circuit LD.dig as structural Verilog
module LD (
  input  [23:0] A,
  input  [23:0] B,
  input  [23:0] C,
  input  [23:0] D,
  input  [23:0] Data,
  input  Enable,
  input  [3:0] Instruction,
  output [23:0] REGA,
  output [23:0] REGB,
  output [23:0] REGC,
  output [23:0] REGD
);

  wire demultiplexer_1_out_0, demultiplexer_1_out_1, demultiplexer_1_out_2, demultiplexer_1_out_3,
       demultiplexer_1_out_4, demultiplexer_1_out_5;
  wire [23:0] multiplexer_1_out, multiplexer_2_out, multiplexer_3_out, multiplexer_4_out, mv_1_p7, mv_1_p8,
       mv_1_p9, mv_1_p10;

  Multiplexer #(.Bits(24)) multiplexer_1 (.sel(demultiplexer_1_out_0), .in_0(A), .in_1(Data), .out(multiplexer_1_out));
  Multiplexer #(.Bits(24)) multiplexer_2 (.sel(demultiplexer_1_out_1), .in_0(B), .in_1(Data), .out(multiplexer_2_out));
  Multiplexer #(.Bits(24)) multiplexer_3 (.sel(demultiplexer_1_out_2), .in_0(C), .in_1(Data), .out(multiplexer_3_out));
  Multiplexer #(.Bits(24)) multiplexer_4 (.sel(demultiplexer_1_out_3), .in_0(D), .in_1(Data), .out(multiplexer_4_out));
  Demultiplexer #(.Selector_Bits(4)) demultiplexer_1 (
    .sel(Instruction), .in(Enable), .out_0(demultiplexer_1_out_0), .out_1(demultiplexer_1_out_1),
    .out_2(demultiplexer_1_out_2), .out_3(demultiplexer_1_out_3), .out_4(demultiplexer_1_out_4),
    .out_5(demultiplexer_1_out_5));  // open: out_6, out_7, out_8, out_9, out_10, out_11, out_12, out_13, out_14, out_15
  // MV mv_1: pin names not known; wires that end beside it: multiplexer_1_out, multiplexer_2_out, multiplexer_3_out, multiplexer_4_out, Data, demultiplexer_1_out_4, mv_1_p7, mv_1_p8, mv_1_p9, mv_1_p10
  SWP swp_1 (
    .A(mv_1_p7), .B(mv_1_p8), .C(mv_1_p9), .D(mv_1_p10), .Data(Data), .Enable(demultiplexer_1_out_5),
    .REGA(REGA), .REGB(REGB), .REGC(REGC), .REGD(REGD));
endmodule
