// Digital circuit SWP.dig as structural Verilog
module SWP (
  input  [23:0] A,
  input  [23:0] B,
  input  [23:0] C,
  input  [23:0] D,
  input  [23:0] Data,
  input  Enable,
  output [23:0] REGA,
  output [23:0] REGB,
  output [23:0] REGC,
  output [23:0] REGD
);

  wire demultiplexer_1_out_0, demultiplexer_1_out_1, demultiplexer_1_out_2;
  wire [23:0] multiplexer_4_out;

  Demultiplexer #(.Selector_Bits(2)) demultiplexer_1 (
    .sel(Data[1:0]), .in(Enable), .out_0(demultiplexer_1_out_0), .out_1(demultiplexer_1_out_1),
    .out_2(demultiplexer_1_out_2));  // open: out_3
  Multiplexer #(.Bits(24)) multiplexer_1 (.sel(demultiplexer_1_out_0), .in_0(B), .in_1(A), .out(REGB));
  Multiplexer #(.Bits(24)) multiplexer_2 (.sel(demultiplexer_1_out_1), .in_0(C), .in_1(A), .out(REGC));
  Multiplexer #(.Bits(24)) multiplexer_3 (.sel(demultiplexer_1_out_2), .in_0(D), .in_1(A), .out(REGD));
  Multiplexer #(.Bits(24), .Selector_Bits(2)) multiplexer_4 (
    .sel(Data[1:0]), .in_0(B), .in_1(C), .in_2(D), .in_3({24{1'b0}}), .out(multiplexer_4_out));
  Multiplexer #(.Bits(24)) multiplexer_5 (.sel(Enable), .in_0(A), .in_1(multiplexer_4_out), .out(REGA));
endmodule
